// Logisim project My_own_cpu.circ as structural Verilog: 18 circuits, main circuit own cpu
module own_cpu (
  input  RESET_PORTS,
  input  CPU_RESET,
  input  REG_RESET,
  output [15:0] out_4
);

  wire ADR_2_out, alu_decoder_1_alu_switch_out, and_3_out, CLK, CLOCK_out, comparator_1_eq, comparator_2_eq,
       comparator_3_eq, comparator_5_eq, comparator_6_eq, DATA_2_out, data_adr_fetch_1_adr,
       data_adr_fetch_1_data_or_reg, DECODE, DECODE_ADR_CLOCK_OUT, DECODE_DATA_CLOCK_OUT, decode_fsm_1_y0,
       decode_fsm_1_y1, DECODE_SW, DR_out_2, EXECUTE, EXECUTE_DATA_CLOCK_OUT, FETCH, FETCH_OUT, FETCH_SW,
       not_1_out, OP_out_2, OPT_R_out, or_2_out, or_3_out, or_4_out, or_5_out, P0_IN, P1_IN, P2_IN, P3_IN,
       P4_IN, P5_IN, P6_IN, P7_IN, P8_IN, SKIP, STOP, WRITE, write_op_decoder_1_don_t_write,
       write_op_decoder_1_ports, write_op_decoder_1_register, write_op_decoder_2_ports,
       write_op_decoder_2_ram, write_op_decoder_2_register, write_reg_port_decoder_2_r0,
       write_reg_port_decoder_2_r1, write_reg_port_decoder_2_r2, write_reg_port_decoder_2_r3, WRITE_RO,
       WRITE_SW;
  wire [1:0] multiplexer_2_out, RAM_MUX;
  wire [2:0] alu_decoder_1_opcode_alu_out;
  wire [3:0] alu_1_flags, D_REG, DR_OUT, OP_T_SR, OPT_OUT;
  wire [7:0] OP_OUT, OPCODE;
  wire [15:0] ADR_IN, ADR_OUT, ALU_OUT, buffer_1_out, DATA_IN, DATA_OUT, DATA_q,
       decoder_data_in_controller_1_out, decoder_data_in_controller_2_out, multiplexer_1_out,
       multiplexer_3_out, multiplexer_4_out, P0_OUT, P1_OUT, P2_OUT, P3_OUT, P4_OUT, P5_OUT, P6_OUT, P7_OUT,
       P8_OUT, PC_DECODER, PC_OUT, ports_data_in_controller_1_out_11, R0_OUT, R1_OUT, R2_OUT, R3_OUT,
       subtractor_1_out, WRITE_PC_LOAD;

  write_op_decoder write_op_decoder_1 (
    .OPCODE(OP_OUT), .RAM(WRITE_RO), .PORTS(write_op_decoder_1_ports),
    .DON_T_WRITE(write_op_decoder_1_don_t_write), .REGISTER(write_op_decoder_1_register), .WRITE_EN(WRITE));
  // Probe on DATA_OUT
  Multiplexer #(.select(2), .width(16), .enable("false")) multiplexer_1 (
    .in0(PC_OUT), .in1(PC_DECODER), .in2(PC_OUT), .in3(PC_OUT), .out(multiplexer_1_out), .sel(RAM_MUX));
  Multiplexer #(.select(2), .width(2), .enable("false")) multiplexer_2 (
    .in0(2'b00), .in1(2'b11), .in2(2'b11), .in3(2'b10), .out(multiplexer_2_out), .sel(RAM_MUX));
  or or_1 (WRITE_SW, WRITE_RO, write_op_decoder_1_ports, write_op_decoder_1_don_t_write, write_op_decoder_1_register);
  Comparator #(.width(4)) comparator_1 (.a(OPT_OUT), .b(4'b1101), .eq(comparator_1_eq));  // open: gt, lt
  or or_2 (or_2_out, comparator_1_eq, comparator_2_eq);
  Comparator #(.width(4)) comparator_2 (.a(OPT_OUT), .b(4'b1010), .eq(comparator_2_eq));  // open: gt, lt
  RAM #(.addrWidth(16), .dataWidth(16), .bus("separate")) ram_1 (
    .addr(multiplexer_1_out), .din(DATA_OUT), .data({OPCODE, OP_T_SR, D_REG}), .clk(WRITE_RO));  // open: str, sel, ld, clr
  ONE_ACTION_FSM one_action_fsm_1 (.CLOCK(CLK), .PHASE(FETCH), .RESET(CPU_RESET), .SWITCH(FETCH_SW), .OUT(FETCH_OUT));
  // Probe on PC_OUT
  custom_counter custom_counter_1 (
    .OPCODE(multiplexer_2_out), .LOAD_VALUE(WRITE_PC_LOAD), .CLOCK(CLK), .RESET(CPU_RESET), .OUTPUT(PC_OUT));
  write_reg_port_decoder write_reg_port_decoder_1 (
    .DEST_REG(DR_OUT), .CLOCK(CLK), .WRITE(write_op_decoder_1_ports), .R0(P0_IN), .R1(P1_IN), .R2(P2_IN),
    .R3(P3_IN), .P4(P4_IN), .P5(P5_IN), .P6(P6_IN), .P7(P7_IN), .P8(P8_IN));
  write_reg_port_decoder write_reg_port_decoder_2 (
    .DEST_REG(DR_OUT), .CLOCK(CLK), .WRITE(write_op_decoder_1_register), .R0(write_reg_port_decoder_2_r0),
    .R1(write_reg_port_decoder_2_r1), .R2(write_reg_port_decoder_2_r2), .R3(write_reg_port_decoder_2_r3));  // open: P4, P5, P6, P7, P8
  Subtractor #(.width(16)) subtractor_1 (.a(PC_OUT), .b(16'h1), .out(subtractor_1_out));  // open: bin, bout
  Multiplexer #(.width(16), .enable("false")) multiplexer_3 (
    .in0(subtractor_1_out), .in1(PC_OUT), .out(multiplexer_3_out), .sel(or_2_out));
  jmp_controller jmp_controller_1 (
    .PC(multiplexer_3_out), .DATA_REGISTER(DATA_OUT), .OPCODE(OP_OUT), .FLAGS(out_4), .OUT(WRITE_PC_LOAD));
  Register #(.width(16), .trigger("falling")) R0 (
    .D(DATA_OUT), .Q(R0_OUT), .clk(write_reg_port_decoder_2_r0), .clr(REG_RESET));  // open: en
  Register #(.width(16), .trigger("falling")) R1 (
    .D(DATA_OUT), .Q(R1_OUT), .clk(write_reg_port_decoder_2_r1), .clr(REG_RESET));  // open: en
  Register #(.width(16), .trigger("falling")) R2 (
    .D(DATA_OUT), .Q(R2_OUT), .clk(write_reg_port_decoder_2_r2), .clr(REG_RESET));  // open: en
  Register #(.width(16), .trigger("falling")) R3 (
    .D(DATA_OUT), .Q(R3_OUT), .clk(write_reg_port_decoder_2_r3), .clr(REG_RESET));  // open: en
  ports_data_in_controller ports_data_in_controller_1 (
    .OPT(OPT_OUT), .P0(P0_OUT), .P1(P1_OUT), .P2(P2_OUT), .P3(P3_OUT), .P4(P4_OUT), .P5(P5_OUT), .P6(P6_OUT),
    .P7(P7_OUT), .P8(P8_OUT), .out_11(ports_data_in_controller_1_out_11));
  decoder_data_in_controller decoder_data_in_controller_1 (
    .OP_TYPE(OPT_OUT), .RAM({OPCODE, OP_T_SR, D_REG}), .R0(R0_OUT), .R1(R1_OUT), .R2(R2_OUT), .R3(R3_OUT),
    .OUT(decoder_data_in_controller_1_out));
  Multiplexer #(.width(16), .enable("false")) multiplexer_4 (
    .in0(decoder_data_in_controller_1_out), .in1(ports_data_in_controller_1_out_11), .out(multiplexer_4_out),
    .sel(comparator_3_eq));
  Comparator comparator_3 (.a(OP_OUT), .b(8'hb), .eq(comparator_3_eq));  // open: gt, lt
  and and_1 (CLK, ~STOP, CLOCK_out);  // AND_Gate
  Clock CLOCK (.out(CLOCK_out));
  // Probe on DATA_IN
  Multiplexer #(.width(16), .enable("false")) multiplexer_5 (
    .in0(ALU_OUT), .in1(multiplexer_4_out), .out(DATA_IN), .sel(DECODE));
  decoder_data_in_controller decoder_data_in_controller_2 (
    .OP_TYPE(DR_OUT), .RAM({16{1'b0}}), .R0(R0_OUT), .R1(R1_OUT), .R2(R2_OUT), .R3(R3_OUT),
    .OUT(decoder_data_in_controller_2_out));
  // Probe on decoder_data_in_controller_2_out
  // Probe on DATA_OUT
  alu_decoder alu_decoder_1 (
    .OPCODE(OP_OUT), .OPCODE_ALU_OUT(alu_decoder_1_opcode_alu_out),
    .ALU_SWITCH_OUT(alu_decoder_1_alu_switch_out));
  Register #(.trigger("falling")) u_OPCODE (.D(OPCODE), .Q(OP_OUT), .clk(OP_out_2), .clr(CPU_RESET));  // open: en
  buf OP (OP_out_2, FETCH_OUT);  // OR_Gate
  buf OPT_R (OPT_R_out, FETCH_OUT);  // OR_Gate
  not not_1 (not_1_out, alu_decoder_1_alu_switch_out);
  // Probe on alu_decoder_1_opcode_alu_out
  data_adr_fetch data_adr_fetch_1 (
    .OP_TYPE(OPT_OUT), .DATA_OR_REG(data_adr_fetch_1_data_or_reg), .ADR(data_adr_fetch_1_adr));
  Comparator comparator_4 (.a(OP_OUT), .b({8{1'b0}}), .eq(SKIP));  // open: gt, lt
  Comparator comparator_5 (.a(OP_OUT), .b({8{1'b1}}), .eq(comparator_5_eq));  // open: gt, lt
  and and_2 (STOP, comparator_5_eq, FETCH);
  PHASE_FSM phase_fsm_1 (
    .CLOCK(CLK), .NEXT_PHASE(or_3_out), .RESET(or_4_out), .FETCH(FETCH), .DECODE(DECODE), .EXECUTE(EXECUTE),
    .WRITE(WRITE));
  or or_3 (or_3_out, FETCH_SW, DECODE_SW, EXECUTE, WRITE_SW);
  or or_4 (or_4_out, CPU_RESET, SKIP);
  Register #(.width(4), .trigger("falling")) OP_TYPE_SREG (
    .D(OP_T_SR), .Q(OPT_OUT), .clk(OPT_R_out), .clr(CPU_RESET));  // open: en
  buf DR (DR_out_2, FETCH_OUT);  // OR_Gate
  // Probe on ALU_OUT
  alu alu_1 (
    .\Вход_А (decoder_data_in_controller_2_out), .in_2(not_1_out), .\Вход_B (DATA_OUT),
    .OPCODE(alu_decoder_1_opcode_alu_out), .\Выход (ALU_OUT), .FLAGS(alu_1_flags));
  D_Flip_Flop #(.trigger("falling")) d_ff_1 (
    .clk(CLK), .D(EXECUTE), .Q(EXECUTE_DATA_CLOCK_OUT), .reset(CPU_RESET));  // open: Qn, preset, en
  DECODE_FSM decode_fsm_1 (
    .CLOCK(CLK), .x0(DECODE), .x1(data_adr_fetch_1_data_or_reg), .x2(data_adr_fetch_1_adr),
    .RESET(CPU_RESET), .y0(decode_fsm_1_y0), .y1(decode_fsm_1_y1), .y2(DECODE_DATA_CLOCK_OUT),
    .y3(DECODE_ADR_CLOCK_OUT), .y4(DECODE_SW));
  Register #(.width(16), .trigger("falling")) DATA (
    .D(buffer_1_out), .Q(DATA_q), .clk(DATA_2_out), .clr(CPU_RESET));  // open: en
  Register #(.width(4), .trigger("falling")) DREG (.D(D_REG), .Q(DR_OUT), .clk(DR_out_2), .clr(CPU_RESET));  // open: en
  assign buffer_1_out = DATA_IN;  // Buffer buffer_1, 16 bits wide
  or DATA_2 (DATA_2_out, DECODE_DATA_CLOCK_OUT, EXECUTE_DATA_CLOCK_OUT);
  write_op_decoder write_op_decoder_2 (
    .OPCODE(OP_OUT), .RAM(write_op_decoder_2_ram), .PORTS(write_op_decoder_2_ports),
    .REGISTER(write_op_decoder_2_register), .WRITE_EN(EXECUTE));  // open: DON_T_WRITE
  or or_5 (or_5_out, write_op_decoder_2_ram, write_op_decoder_2_ports, write_op_decoder_2_register, and_3_out);
  and and_3 (and_3_out, EXECUTE, comparator_6_eq);
  Comparator comparator_6 (.a(OP_OUT), .b(8'h4), .eq(comparator_6_eq));  // open: gt, lt
  Multiplexer #(.width(16), .enable("false")) multiplexer_6 (
    .in0(PC_OUT), .in1(ADR_OUT), .out(PC_DECODER), .sel(decode_fsm_1_y0));
  // Probe on PC_DECODER
  // Probe on ADR_IN
  Multiplexer #(.width(16), .enable("false")) multiplexer_7 (
    .in0({OPCODE, OP_T_SR, D_REG}), .in1(PC_OUT), .out(ADR_IN), .sel(decode_fsm_1_y1));
  assign DATA_OUT = DATA_q;  // Buffer buffer_2, 16 bits wide
  Register #(.width(16), .trigger("falling")) ADR (
    .D(ADR_IN), .Q(ADR_OUT), .clk(ADR_2_out), .clr(CPU_RESET));  // open: en
  buf ADR_2 (ADR_2_out, DECODE_ADR_CLOCK_OUT);  // OR_Gate
  Register #(.width(16)) PS__FLAGS (.D({{12{1'b0}}, alu_1_flags}), .Q(out_4), .clk(or_5_out));  // open: en, clr
  assign RAM_MUX = 2'b00 | {1'b0, DECODE} | {EXECUTE, 1'b0} | {2{WRITE}};  // OR_Gate or_6, 2 bits wide
  Register #(.width(16), .trigger("falling")) P0 (
    .D(DATA_OUT), .Q(P0_OUT), .clk(P0_IN), .clr(RESET_PORTS));  // open: en
  Register #(.width(16), .trigger("falling")) P1 (
    .D(DATA_OUT), .Q(P1_OUT), .clk(P1_IN), .clr(RESET_PORTS));  // open: en
  Register #(.width(16), .trigger("falling")) P2 (
    .D(DATA_OUT), .Q(P2_OUT), .clk(P2_IN), .clr(RESET_PORTS));  // open: en
  Register #(.width(16), .trigger("falling")) P3 (
    .D(DATA_OUT), .Q(P3_OUT), .clk(P3_IN), .clr(RESET_PORTS));  // open: en
  Register #(.width(16), .trigger("falling")) P4 (
    .D(DATA_OUT), .Q(P4_OUT), .clk(P4_IN), .clr(RESET_PORTS));  // open: en
  Register #(.width(16), .trigger("falling")) P5 (
    .D(DATA_OUT), .Q(P5_OUT), .clk(P5_IN), .clr(RESET_PORTS));  // open: en
  Register #(.width(16), .trigger("falling")) P6 (
    .D(DATA_OUT), .Q(P6_OUT), .clk(P6_IN), .clr(RESET_PORTS));  // open: en
  Register #(.width(16), .trigger("falling")) P7 (
    .D(DATA_OUT), .Q(P7_OUT), .clk(P7_IN), .clr(RESET_PORTS));  // open: en
  Register #(.width(16), .trigger("falling")) P8 (
    .D(DATA_OUT), .Q(P8_OUT), .clk(P8_IN), .clr(RESET_PORTS));  // open: en
  DotMatrix #(.inputtype("row"), .matrixcols(16), .matrixrows(9)) dotmatrix_1 (
    .row0(P0_OUT), .row1(P1_OUT), .row2(P2_OUT), .row3(P3_OUT), .row4(P4_OUT), .row5(P5_OUT), .row6(P6_OUT),
    .row7(P7_OUT), .row8(P8_OUT));

  // Other names for the same wires on the sheet: EXECUTE_SW = EXECUTE; PC_WRITE[15:0] = PC_OUT; PS_OUT[15:0] = out_4;
  //   RAM_OUT[15:0] = {OPCODE, OP_T_SR, D_REG}; RES = CPU_RESET

  // Notes on the sheet:
  //   RAM
  //   FETCH FSM
  //   SERVICE REG
  //   CORE
  //   DECODER
  //   PHASE FSM
  //   PC SELECTOR
  //   ADR IN SELECTOR
  //   OCZN
  //   P0 P1 P2 P3 P4 P5 P6 P7 P8
endmodule

module PHASE_FSM (
  input  CLOCK,
  input  NEXT_PHASE,
  input  RESET,
  output FETCH,
  output DECODE,
  output EXECUTE,
  output WRITE
);

  wire and_1_out, and_2_out, and_3_out, and_4_out, not_1_out, not_2_out, not_3_out, not_4_out, not_5_out,
       not_6_out, or_1_out, or_2_out, t_ff_1_q, t_ff_2_q;

  not not_1 (not_1_out, 1'b0);
  not not_2 (not_2_out, 1'b0);
  and and_1 (and_1_out, t_ff_2_q, NEXT_PHASE, not_1_out);
  or or_1 (or_1_out, and_1_out, and_2_out);
  and and_2 (and_2_out, t_ff_1_q, 1'b0);
  and and_3 (and_3_out, NEXT_PHASE, not_2_out);
  or or_2 (or_2_out, and_3_out, and_4_out);
  and and_4 (and_4_out, t_ff_2_q, 1'b0);
  T_Flip_Flop t_ff_1 (.clk(CLOCK), .T(or_1_out), .Q(t_ff_1_q), .reset(RESET));  // open: Qn, preset, en
  T_Flip_Flop t_ff_2 (.clk(CLOCK), .T(or_2_out), .Q(t_ff_2_q), .reset(RESET));  // open: Qn, preset, en
  not not_3 (not_3_out, t_ff_1_q);
  not not_4 (not_4_out, t_ff_2_q);
  not not_5 (not_5_out, t_ff_1_q);
  not not_6 (not_6_out, t_ff_2_q);
  and and_5 (WRITE, t_ff_1_q, t_ff_2_q);
  and and_6 (FETCH, not_3_out, not_4_out);
  and and_7 (DECODE, not_5_out, t_ff_2_q);
  and and_8 (EXECUTE, t_ff_1_q, not_6_out);

  // Notes on the sheet:
  //   Delta
  //   Lambda
endmodule

module ONE_ACTION_FSM (
  input  CLOCK,
  input  PHASE,
  input  RESET,
  output SWITCH,
  output OUT
);

  wire d_ff_1_q;

  and and_1 (OUT, CLOCK, PHASE);
  D_Flip_Flop d_ff_1 (.clk(CLOCK), .D(PHASE), .Q(d_ff_1_q), .reset(RESET));  // open: Qn, preset, en
  and and_2 (SWITCH, d_ff_1_q, PHASE);

  // Notes on the sheet:
  //   ONE ACTION FSM
endmodule

module DECODE_FSM (
  input  CLOCK,
  input  x0,
  input  x1,
  input  x2,
  input  RESET,
  output y0,
  output y1,
  output y2,
  output y3,
  output y4
);

  wire and_1_out, and_2_out, and_3_out, and_4_out, and_5_out, and_6_out, and_7_out, and_8_out, and_9_out,
       and_12_out, and_13_out, not_1_out, not_2_out, not_3_out, not_4_out, not_5_out, not_6_out, not_7_out,
       not_8_out, not_9_out, not_10_out, not_11_out, not_12_out, not_13_out, not_14_out, not_15_out,
       not_16_out, or_1_out, or_2_out, or_3_out, t_ff_2_q;

  not not_1 (not_1_out, t_ff_2_q);
  not not_2 (not_2_out, x2);
  not not_3 (not_3_out, x1);
  not not_4 (not_4_out, y4);
  not not_5 (not_5_out, t_ff_2_q);
  not not_6 (not_6_out, y2);
  not not_7 (not_7_out, x1);
  not not_8 (not_8_out, x0);
  not not_9 (not_9_out, x2);
  not not_10 (not_10_out, y4);
  not not_11 (not_11_out, t_ff_2_q);
  not not_12 (not_12_out, x2);
  not not_13 (not_13_out, x1);
  and and_1 (and_1_out, not_1_out, y2, x0, x1, not_2_out);
  and and_2 (and_2_out, t_ff_2_q, y2, x0, not_3_out, x2);
  or or_1 (or_1_out, and_1_out, and_2_out, y4);
  and and_3 (and_3_out, not_4_out, not_5_out, not_6_out, x0, not_7_out, x2);
  and and_4 (and_4_out, t_ff_2_q, not_8_out);
  and and_5 (and_5_out, t_ff_2_q, not_9_out);
  and and_6 (and_6_out, t_ff_2_q, x1);
  and and_7 (and_7_out, t_ff_2_q, y2);
  and and_8 (and_8_out, not_10_out, not_11_out, x0, x1, not_12_out);
  or or_2 (or_2_out, and_8_out, y2, and_9_out);
  and and_9 (and_9_out, t_ff_2_q, x0, not_13_out, x2);
  or or_3 (or_3_out, and_3_out, and_4_out, and_5_out, and_6_out, and_7_out);
  T_Flip_Flop t_ff_1 (.clk(CLOCK), .T(or_1_out), .Q(y4), .reset(RESET));  // open: Qn, preset, en
  T_Flip_Flop t_ff_2 (.clk(CLOCK), .T(or_3_out), .Q(t_ff_2_q), .reset(RESET));  // open: Qn, preset, en
  T_Flip_Flop t_ff_3 (.clk(CLOCK), .T(or_2_out), .Q(y2), .reset(RESET));  // open: Qn, preset, en
  and and_10 (y0, t_ff_2_q, y2);
  not not_14 (not_14_out, t_ff_2_q);
  not not_15 (not_15_out, t_ff_2_q);
  not not_16 (not_16_out, y2);
  and and_11 (y1, not_14_out, y2);
  and and_12 (and_12_out, not_15_out, y2);
  and and_13 (and_13_out, t_ff_2_q, not_16_out);
  or or_4 (y3, and_12_out, and_13_out);

  // Notes on the sheet:
  //   Delta
  //   Lambda
endmodule

module alu (
  input  [15:0] \Вход_А ,
  input  in_2,
  input  [15:0] \Вход_B ,
  input  [2:0] OPCODE,
  output [15:0] \Выход ,
  output [3:0] FLAGS
);

  wire bitselector_1_out, bitselector_2_out, not_1_out, or_2_out, xnor_1_out, xor_1_out;
  wire [15:0] adder_1_out, and_1_out, buffer_1_out, multiplexer_1_out, multiplexer_2_out, not_2_out,
       or_1_out, shifter_1_out, shifter_2_out, subtractor_1_out;

  // Probe on \Вход_А 
  // Probe on \Вход_B 
  Multiplexer #(.width(16), .enable("false")) multiplexer_1 (
    .in0(\Вход_А ), .in1(\Вход_B ), .out(multiplexer_1_out), .sel(in_2));
  not not_1 (not_1_out, in_2);
  Multiplexer #(.width(16), .enable("false")) multiplexer_2 (
    .in0(\Вход_А ), .in1(\Вход_B ), .out(multiplexer_2_out), .sel(not_1_out));
  assign buffer_1_out = multiplexer_1_out;  // Buffer buffer_1, 16 bits wide
  Adder #(.width(16)) adder_1 (
    .a(multiplexer_2_out), .b(multiplexer_1_out), .out(adder_1_out), .cout(FLAGS[2]));  // open: cin
  Subtractor #(.width(16)) subtractor_1 (
    .a(multiplexer_2_out), .b(multiplexer_1_out), .out(subtractor_1_out));  // open: bin, bout
  assign not_2_out = ~multiplexer_1_out;  // NOT_Gate not_2, 16 bits wide
  assign and_1_out = multiplexer_1_out & multiplexer_2_out;  // AND_Gate and_1, 16 bits wide
  assign or_1_out = multiplexer_1_out | multiplexer_2_out;  // OR_Gate or_1, 16 bits wide
  Shifter #(.width(16)) shifter_1 (.in(multiplexer_1_out), .\dist (4'b0001), .out(shifter_1_out));
  Shifter #(.width(16), .shift("ar")) shifter_2 (.in(multiplexer_1_out), .\dist (4'b0001), .out(shifter_2_out));
  Multiplexer #(.select(3), .width(16), .enable("false")) multiplexer_3 (
    .in0(buffer_1_out), .in1(adder_1_out), .in2(subtractor_1_out), .in3(not_2_out), .in4(and_1_out),
    .in5(or_1_out), .in6(shifter_1_out), .in7(shifter_2_out), .out({FLAGS[0], \Выход [14:0]}), .sel(OPCODE));
  BitSelector #(.width(16)) bitselector_1 (.in(multiplexer_2_out), .out(bitselector_1_out), .sel(4'b1111));
  // Probe on {FLAGS[0], \Выход [14:0]}
  BitSelector #(.width(16)) bitselector_2 (.in(multiplexer_1_out), .out(bitselector_2_out), .sel(4'b1111));
  xor xor_1 (xor_1_out, FLAGS[0], bitselector_2_out);
  and and_2 (FLAGS[3], xor_1_out, xnor_1_out);
  xnor xnor_1 (xnor_1_out, bitselector_2_out, bitselector_1_out);
  not not_3 (FLAGS[1], or_2_out);
  or or_2 (or_2_out, FLAGS[0], \Выход [14], \Выход [13], \Выход [12], \Выход [11], \Выход [10], \Выход [9], \Выход [8], \Выход [7], \Выход [6], \Выход [5], \Выход [4], \Выход [3], \Выход [2], \Выход [1], \Выход [0]);

  assign \Выход [15] = FLAGS[0];

  // Notes on the sheet:
  //   000 - buffer
  //   001 - add
  //   010 - sub
  //   011 - not
  //   100 - and
  //   101 - or
  //   110 - logical left
  //   111 - arithmetic right 
  //   16-bit ALU
  //   OCZN
  //   OCZN
endmodule

module custom_counter (
  input  [1:0] OPCODE,
  input  [15:0] LOAD_VALUE,
  input  CLOCK,
  input  RESET,
  output [15:0] OUTPUT
);

  wire and_1_out;
  wire [15:0] adder_1_out, multiplexer_1_out, multiplexer_2_out;

  Multiplexer #(.width(16), .enable("false")) multiplexer_1 (
    .in0(OUTPUT), .in1({16{1'b0}}), .out(multiplexer_1_out), .sel(and_1_out));
  Multiplexer #(.select(2), .width(16), .enable("false")) multiplexer_2 (
    .in0(16'h1), .in1(16'h2), .in2(LOAD_VALUE), .out(multiplexer_2_out), .sel(OPCODE));  // open: in3
  and and_1 (and_1_out, ~OPCODE[0], OPCODE[1]);  // AND_Gate
  Adder #(.width(16)) adder_1 (.a(multiplexer_1_out), .b(multiplexer_2_out), .out(adder_1_out));  // open: cin, cout
  Register #(.width(16)) register_1 (.D(adder_1_out), .Q(OUTPUT), .clk(CLOCK), .clr(RESET));  // open: en

  // Notes on the sheet:
  //   COMMANDS
  //   00 - default mode +1
  //   01 - double increment +2
  //   10 - load value
  //   11 - halt value
  //   CUSTOM COUNTER
endmodule

module data_adr_fetch (
  input  [3:0] OP_TYPE,
  output DATA_OR_REG,
  output ADR
);

  wire and_1_out, comparator_1_eq;

  // Probe on OP_TYPE
  Comparator #(.width(4)) comparator_1 (.a(OP_TYPE), .b(4'b1101), .eq(comparator_1_eq));  // open: gt, lt
  Comparator #(.width(4)) comparator_2 (.a(OP_TYPE), .b(4'b1010), .eq(ADR));  // open: gt, lt
  and and_1 (and_1_out, ~comparator_1_eq, ~ADR);  // AND_Gate
  or or_1 (DATA_OR_REG, comparator_1_eq, and_1_out);
endmodule

module decoder_data_in_controller (
  input  [3:0] OP_TYPE,
  input  [15:0] RAM,
  input  [15:0] R0,
  input  [15:0] R1,
  input  [15:0] R2,
  input  [15:0] R3,
  output [15:0] OUT
);

  wire and_2_out, and_3_out, not_1_out, not_2_out, not_3_out, not_4_out, not_5_out, not_6_out, not_7_out,
       not_8_out, not_9_out, not_10_out, not_11_out;
  wire [2:0] and_4_out;

  not not_1 (not_1_out, OP_TYPE[3]);
  not not_2 (not_2_out, OP_TYPE[2]);
  not not_3 (not_3_out, OP_TYPE[3]);
  not not_4 (not_4_out, OP_TYPE[2]);
  not not_5 (not_5_out, OP_TYPE[1]);
  not not_6 (not_6_out, OP_TYPE[3]);
  not not_7 (not_7_out, OP_TYPE[2]);
  not not_8 (not_8_out, OP_TYPE[0]);
  not not_9 (not_9_out, OP_TYPE[3]);
  not not_10 (not_10_out, OP_TYPE[2]);
  not not_11 (not_11_out, OP_TYPE[0]);
  and and_1 (and_4_out[2], not_1_out, not_2_out, OP_TYPE[1], OP_TYPE[0]);
  and and_2 (and_2_out, not_3_out, not_4_out, not_5_out, OP_TYPE[0]);
  and and_3 (and_3_out, not_6_out, not_7_out, OP_TYPE[1], not_8_out);
  and and_4 (and_4_out[0], not_9_out, not_10_out, not_11_out);
  Multiplexer #(.select(3), .width(16), .enable("false")) multiplexer_1 (
    .in0(RAM), .in1(R0), .in2(R1), .in3(R2), .in4(R3), .out(OUT), .sel(and_4_out));  // open: in5, in6, in7
  or or_1 (and_4_out[1], and_2_out, and_3_out);
endmodule

module ports_data_in_controller (
  input  [3:0] OPT,
  input  [15:0] P0,
  input  [15:0] P1,
  input  [15:0] P2,
  input  [15:0] P3,
  input  [15:0] P4,
  input  [15:0] P5,
  input  [15:0] P6,
  input  [15:0] P7,
  input  [15:0] P8,
  output [15:0] out_11
);

  Multiplexer #(.select(4), .width(16), .enable("false")) multiplexer_1 (
    .in0(P0), .in1(P1), .in2(P2), .in3(P3), .in4(P4), .in5(P5), .in6(P6), .in7(P7), .in8(P8),
    .in9({16{1'b0}}), .in10({16{1'b0}}), .in11({16{1'b0}}), .in12({16{1'b0}}), .in13({16{1'b0}}),
    .in14({16{1'b0}}), .in15({16{1'b0}}), .out(out_11), .sel(OPT));
endmodule

module alu_decoder (
  input  [7:0] OPCODE,
  output [2:0] OPCODE_ALU_OUT,
  output ALU_SWITCH_OUT
);

  wire and_1_out, and_2_out, and_3_out, and_4_out, and_5_out, and_6_out, and_7_out, and_8_out, not_1_out,
       not_2_out, not_3_out, not_4_out, not_5_out, not_6_out, not_7_out, not_8_out, not_9_out, not_10_out,
       not_11_out, not_12_out, not_13_out, not_14_out, not_15_out, not_16_out, not_17_out, not_18_out,
       not_19_out, not_20_out, not_21_out, not_22_out, not_23_out, not_24_out, not_25_out, not_26_out,
       not_27_out, not_28_out, not_29_out, not_30_out, not_31_out, not_32_out, not_33_out, not_34_out,
       not_35_out, not_36_out, not_37_out, not_38_out, not_39_out, not_40_out, not_41_out, not_42_out,
       not_43_out, not_44_out, not_45_out, not_46_out, not_47_out, not_48_out, not_49_out, not_50_out,
       not_51_out, not_52_out, not_53_out, not_54_out;

  not not_1 (not_1_out, OPCODE[7]);
  not not_2 (not_2_out, OPCODE[6]);
  not not_3 (not_3_out, OPCODE[5]);
  not not_4 (not_4_out, OPCODE[4]);
  not not_5 (not_5_out, OPCODE[3]);
  not not_6 (not_6_out, OPCODE[7]);
  not not_7 (not_7_out, OPCODE[6]);
  not not_8 (not_8_out, OPCODE[5]);
  not not_9 (not_9_out, OPCODE[4]);
  not not_10 (not_10_out, OPCODE[2]);
  not not_11 (not_11_out, OPCODE[1]);
  not not_12 (not_12_out, OPCODE[7]);
  not not_13 (not_13_out, OPCODE[6]);
  not not_14 (not_14_out, OPCODE[5]);
  not not_15 (not_15_out, OPCODE[4]);
  not not_16 (not_16_out, OPCODE[3]);
  not not_17 (not_17_out, OPCODE[2]);
  not not_18 (not_18_out, OPCODE[7]);
  not not_19 (not_19_out, OPCODE[6]);
  not not_20 (not_20_out, OPCODE[5]);
  not not_21 (not_21_out, OPCODE[4]);
  not not_22 (not_22_out, OPCODE[3]);
  not not_23 (not_23_out, OPCODE[1]);
  not not_24 (not_24_out, OPCODE[7]);
  not not_25 (not_25_out, OPCODE[6]);
  not not_26 (not_26_out, OPCODE[5]);
  not not_27 (not_27_out, OPCODE[4]);
  not not_28 (not_28_out, OPCODE[2]);
  not not_29 (not_29_out, OPCODE[1]);
  not not_30 (not_30_out, OPCODE[7]);
  not not_31 (not_31_out, OPCODE[6]);
  not not_32 (not_32_out, OPCODE[5]);
  not not_33 (not_33_out, OPCODE[4]);
  not not_34 (not_34_out, OPCODE[3]);
  not not_35 (not_35_out, OPCODE[2]);
  not not_36 (not_36_out, OPCODE[0]);
  not not_37 (not_37_out, OPCODE[7]);
  not not_38 (not_38_out, OPCODE[6]);
  not not_39 (not_39_out, OPCODE[5]);
  not not_40 (not_40_out, OPCODE[4]);
  not not_41 (not_41_out, OPCODE[3]);
  not not_42 (not_42_out, OPCODE[7]);
  not not_43 (not_43_out, OPCODE[6]);
  not not_44 (not_44_out, OPCODE[5]);
  not not_45 (not_45_out, OPCODE[4]);
  not not_46 (not_46_out, OPCODE[2]);
  not not_47 (not_47_out, OPCODE[1]);
  not not_48 (not_48_out, OPCODE[7]);
  not not_49 (not_49_out, OPCODE[6]);
  not not_50 (not_50_out, OPCODE[5]);
  not not_51 (not_51_out, OPCODE[4]);
  not not_52 (not_52_out, OPCODE[3]);
  not not_53 (not_53_out, OPCODE[1]);
  not not_54 (not_54_out, OPCODE[0]);
  and and_1 (and_1_out, not_1_out, not_2_out, not_3_out, not_4_out, not_5_out, OPCODE[2], OPCODE[1]);
  and and_2 (and_2_out, not_6_out, not_7_out, not_8_out, not_9_out, OPCODE[3], not_10_out, not_11_out);
  and and_3 (and_3_out, not_12_out, not_13_out, not_14_out, not_15_out, not_16_out, not_17_out, OPCODE[1], OPCODE[0]);
  and and_4 (and_4_out, not_18_out, not_19_out, not_20_out, not_21_out, not_22_out, OPCODE[2], not_23_out);
  and and_5 (and_5_out, not_24_out, not_25_out, not_26_out, not_27_out, OPCODE[3], not_28_out, not_29_out);
  and and_6 (and_6_out, not_30_out, not_31_out, not_32_out, not_33_out, not_34_out, not_35_out, OPCODE[1], not_36_out);
  and and_7 (and_7_out, not_37_out, not_38_out, not_39_out, not_40_out, not_41_out, OPCODE[2], OPCODE[0]);
  and and_8 (and_8_out, not_42_out, not_43_out, not_44_out, not_45_out, OPCODE[3], not_46_out, not_47_out, OPCODE[0]);
  and and_9 (ALU_SWITCH_OUT, not_48_out, not_49_out, not_50_out, not_51_out, not_52_out, OPCODE[2], not_53_out, not_54_out);
  or or_1 (OPCODE_ALU_OUT[2], and_1_out, and_2_out);
  or or_2 (OPCODE_ALU_OUT[1], and_3_out, and_4_out, and_5_out);
  or or_3 (OPCODE_ALU_OUT[0], and_6_out, and_7_out, and_8_out);
endmodule

module write_op_decoder (
  input  [7:0] OPCODE,
  input  WRITE_EN,
  output RAM,
  output PORTS,
  output DON_T_WRITE,
  output REGISTER
);

  wire and_1_out, comparator_1_eq, comparator_2_eq, comparator_3_gt, comparator_4_lt, comparator_5_eq,
       nor_1_out, or_1_out;

  // Probe on OPCODE
  Comparator comparator_1 (.a(OPCODE), .b(8'h13), .eq(comparator_1_eq));  // open: gt, lt
  Comparator comparator_2 (.a(OPCODE), .b(8'ha), .eq(comparator_2_eq));  // open: gt, lt
  Comparator comparator_3 (.a(OPCODE), .b(8'hb), .gt(comparator_3_gt));  // open: eq, lt
  Comparator comparator_4 (.a(OPCODE), .b(8'h13), .lt(comparator_4_lt));  // open: gt, eq
  Comparator comparator_5 (.a(OPCODE), .b(8'h4), .eq(comparator_5_eq));  // open: gt, lt
  and and_1 (and_1_out, comparator_3_gt, comparator_4_lt);
  or or_1 (or_1_out, and_1_out, comparator_5_eq);
  nor nor_1 (nor_1_out, or_1_out, comparator_2_eq, comparator_1_eq);
  and and_2 (RAM, comparator_1_eq, WRITE_EN);
  and and_3 (PORTS, comparator_2_eq, WRITE_EN);
  and and_4 (DON_T_WRITE, or_1_out, WRITE_EN);
  and and_5 (REGISTER, nor_1_out, WRITE_EN);
endmodule

module write_reg_port_decoder (
  input  [3:0] DEST_REG,
  input  CLOCK,
  input  WRITE,
  output R0,
  output R1,
  output R2,
  output R3,
  output P4,
  output P5,
  output P6,
  output P7,
  output P8
);

  wire and_1_out, and_2_out, and_3_out, and_4_out, and_5_out, and_6_out, and_7_out, and_8_out, and_9_out,
       decoder_1_out0, decoder_1_out1, decoder_1_out2, decoder_1_out3, decoder_1_out4, decoder_1_out5,
       decoder_1_out6, decoder_1_out7, decoder_1_out8;

  Decoder #(.select(4), .enable("false")) decoder_1 (
    .out0(decoder_1_out0), .out1(decoder_1_out1), .out2(decoder_1_out2), .out3(decoder_1_out3),
    .out4(decoder_1_out4), .out5(decoder_1_out5), .out6(decoder_1_out6), .out7(decoder_1_out7),
    .out8(decoder_1_out8), .sel(DEST_REG));  // open: out9, out10, out11, out12, out13, out14, out15
  and and_1 (and_1_out, decoder_1_out0, CLOCK);
  and and_2 (and_2_out, decoder_1_out1, CLOCK);
  and and_3 (and_3_out, decoder_1_out2, CLOCK);
  and and_4 (and_4_out, decoder_1_out3, CLOCK);
  and and_5 (and_5_out, decoder_1_out4, CLOCK);
  and and_6 (and_6_out, decoder_1_out5, CLOCK);
  and and_7 (and_7_out, decoder_1_out6, CLOCK);
  and and_8 (and_8_out, decoder_1_out7, CLOCK);
  and and_9 (and_9_out, decoder_1_out8, CLOCK);
  and and_10 (R0, and_1_out, WRITE);
  and and_11 (R1, and_2_out, WRITE);
  and and_12 (R2, and_3_out, WRITE);
  and and_13 (R3, and_4_out, WRITE);
  and and_14 (P4, and_5_out, WRITE);
  and and_15 (P5, and_6_out, WRITE);
  and and_16 (P6, and_7_out, WRITE);
  and and_17 (P7, and_8_out, WRITE);
  and and_18 (P8, and_9_out, WRITE);
endmodule

module jmp_controller (
  input  [15:0] PC,
  input  [15:0] DATA_REGISTER,
  input  [7:0] OPCODE,
  input  [15:0] FLAGS,
  output [15:0] OUT
);

  wire and_1_out, comparator_1_eq, comparator_2_eq, comparator_3_eq, comparator_4_eq, comparator_5_eq,
       comparator_6_eq, comparator_7_eq, or_1_out;
  wire [0:0] and_2_out;
  wire [1:1] and_3_out, and_4_out;
  wire [2:0] or_2_out;
  wire [2:2] and_5_out, and_6_out, and_7_out, and_8_out;
  wire [3:0] bitselector_1_out;
  wire [15:0] multiplexer_1_out, multiplexer_2_out, multiplexer_3_out, multiplexer_4_out, multiplexer_5_out,
       multiplexer_6_out, multiplexer_7_out;

  Comparator comparator_1 (.a(OPCODE), .b(8'hc), .eq(comparator_1_eq));  // open: gt, lt
  Comparator comparator_2 (.a(OPCODE), .b(8'hd), .eq(comparator_2_eq));  // open: gt, lt
  Comparator comparator_3 (.a(OPCODE), .b(8'he), .eq(comparator_3_eq));  // open: gt, lt
  Comparator comparator_4 (.a(OPCODE), .b(8'hf), .eq(comparator_4_eq));  // open: gt, lt
  Comparator comparator_5 (.a(OPCODE), .b(8'h10), .eq(comparator_5_eq));  // open: gt, lt
  Comparator comparator_6 (.a(OPCODE), .b(8'h11), .eq(comparator_6_eq));  // open: gt, lt
  Comparator comparator_7 (.a(OPCODE), .b(8'h12), .eq(comparator_7_eq));  // open: gt, lt
  and and_1 (and_1_out, bitselector_1_out[3], bitselector_1_out[0]);
  BitSelector #(.width(16), .group(4)) bitselector_1 (.in(FLAGS), .out(bitselector_1_out), .sel(2'b00));
  or or_1 (or_1_out, ~and_1_out, bitselector_1_out[1]);  // OR_Gate
  and and_2 (and_2_out[0], comparator_2_eq, ~bitselector_1_out[1]);  // AND_Gate
  and and_3 (and_3_out[1], comparator_3_eq, bitselector_1_out[1]);
  and and_4 (and_4_out[1], comparator_4_eq, and_1_out, bitselector_1_out[1]);
  and and_5 (and_5_out[2], comparator_5_eq, and_1_out);
  and and_6 (and_6_out[2], comparator_6_eq, ~and_1_out);  // AND_Gate
  and and_7 (and_7_out[2], comparator_7_eq, or_1_out);
  Multiplexer #(.width(16), .enable("false")) multiplexer_1 (
    .in0(PC), .in1(DATA_REGISTER), .out(multiplexer_1_out), .sel(comparator_1_eq));
  Multiplexer #(.width(16), .enable("false")) multiplexer_2 (
    .in0(PC), .in1(DATA_REGISTER), .out(multiplexer_2_out), .sel(and_2_out[0]));
  Multiplexer #(.width(16), .enable("false")) multiplexer_3 (
    .in0(PC), .in1(DATA_REGISTER), .out(multiplexer_3_out), .sel(and_3_out[1]));
  Multiplexer #(.width(16), .enable("false")) multiplexer_4 (
    .in0(PC), .in1(DATA_REGISTER), .out(multiplexer_4_out), .sel(and_4_out[1]));
  Multiplexer #(.width(16), .enable("false")) multiplexer_5 (
    .in0(PC), .in1(DATA_REGISTER), .out(multiplexer_5_out), .sel(and_5_out[2]));
  Multiplexer #(.width(16), .enable("false")) multiplexer_6 (
    .in0(PC), .in1(DATA_REGISTER), .out(multiplexer_6_out), .sel(and_6_out[2]));
  Multiplexer #(.width(16), .enable("false")) multiplexer_7 (
    .in0(PC), .in1(DATA_REGISTER), .out(multiplexer_7_out), .sel(and_7_out[2]));
  and and_8 (and_8_out[2], and_7_out[2], and_6_out[2], and_5_out[2], and_4_out[1], and_3_out[1], and_2_out[0], comparator_1_eq);
  Multiplexer #(.select(3), .width(16), .enable("false")) multiplexer_8 (
    .in0(multiplexer_1_out), .in1(multiplexer_2_out), .in2(multiplexer_3_out), .in3(multiplexer_4_out),
    .in4(multiplexer_5_out), .in5(multiplexer_6_out), .in6(multiplexer_7_out), .in7(PC), .out(OUT),
    .sel(or_2_out));
  assign or_2_out = 3'b000 | {2'b00, and_2_out[0]} | {1'b0, and_3_out[1], 1'b0} | {1'b0, {2{and_4_out[1]}}} | {and_5_out[2], 2'b00} | {and_6_out[2], 1'b0, and_6_out[2]} | {{2{and_7_out[2]}}, 1'b0} | {3{and_8_out[2]}};  // OR_Gate or_2, 3 bits wide

  // Notes on the sheet:
  //   jmp
  //   jnz
  //   jz
  //   jg
  //   jge
  //   jl
  //   jle
  //   OCZN
endmodule

module char_detection (
  input  CLOCK,
  input  RESET,
  input  CARRY,
  input  [6:0] IN,
  input  [6:0] CONST,
  output OUT
);

  wire and_1_out, comparator_1_eq;

  and and_1 (and_1_out, CARRY, comparator_1_eq);
  Comparator #(.width(7)) comparator_1 (.a(IN), .b(CONST), .eq(comparator_1_eq));  // open: gt, lt
  D_Flip_Flop d_ff_1 (.clk(CLOCK), .D(and_1_out), .Q(OUT), .reset(RESET));  // open: Qn, preset, en
endmodule

module word_detection (
  input  RESET,
  input  CLOCK,
  input  [6:0] CHAR,
  input  [27:0] WORD_CODE,
  output OUT
);

  wire char_detection_1_out, char_detection_2_out, char_detection_3_out, char_detection_4_out,
       comparator_1_eq, comparator_2_eq, comparator_3_eq;
  wire [1:0] and_2_out;

  Comparator #(.width(7)) comparator_1 (.a(WORD_CODE[13:7]), .b(7'b0111011), .eq(comparator_1_eq));  // open: gt, lt
  Comparator #(.width(7)) comparator_2 (.a(WORD_CODE[20:14]), .b(7'b0111011), .eq(comparator_2_eq));  // open: gt, lt
  Comparator #(.width(7)) comparator_3 (.a(WORD_CODE[27:21]), .b(7'b0111011), .eq(comparator_3_eq));  // open: gt, lt
  char_detection char_detection_1 (
    .CLOCK(CLOCK), .RESET(RESET), .CARRY(1'b1), .IN(CHAR), .CONST(WORD_CODE[6:0]), .OUT(char_detection_1_out));
  char_detection char_detection_2 (
    .CLOCK(CLOCK), .RESET(RESET), .CARRY(char_detection_1_out), .IN(CHAR), .CONST(WORD_CODE[13:7]),
    .OUT(char_detection_2_out));
  char_detection char_detection_3 (
    .CLOCK(CLOCK), .RESET(RESET), .CARRY(char_detection_2_out), .IN(CHAR), .CONST(WORD_CODE[20:14]),
    .OUT(char_detection_3_out));
  char_detection char_detection_4 (
    .CLOCK(CLOCK), .RESET(RESET), .CARRY(char_detection_3_out), .IN(CHAR), .CONST(WORD_CODE[27:21]),
    .OUT(char_detection_4_out));
  and and_1 (and_2_out[1], ~comparator_1_eq, ~comparator_2_eq);  // AND_Gate
  and and_2 (and_2_out[0], ~comparator_1_eq, ~comparator_3_eq);  // AND_Gate
  Multiplexer #(.select(2), .enable("false")) multiplexer_1 (
    .in0(char_detection_1_out), .in1(char_detection_2_out), .in2(char_detection_3_out),
    .in3(char_detection_4_out), .out(OUT), .sel(and_2_out));
endmodule

module OP_KEYBOARD (
  input  [6:0] KB_IN,
  input  CLOCK,
  input  RESET,
  output [7:0] OP_OUT
);

  wire word_detection_1_out, word_detection_2_out, word_detection_3_out, word_detection_4_out,
       word_detection_5_out, word_detection_6_out, word_detection_7_out, word_detection_8_out,
       word_detection_9_out, word_detection_10_out, word_detection_11_out, word_detection_12_out,
       word_detection_13_out, word_detection_14_out, word_detection_15_out, word_detection_16_out,
       word_detection_17_out, word_detection_18_out, word_detection_19_out;
  wire [4:0] or_1_out;

  // Probe on KB_IN
  word_detection word_detection_1 (
    .RESET(RESET), .CLOCK(CLOCK), .CHAR(KB_IN), .WORD_CODE(28'h77db7ed), .OUT(word_detection_1_out));
  word_detection word_detection_2 (
    .RESET(RESET), .CLOCK(CLOCK), .CHAR(KB_IN), .WORD_CODE(28'h7793261), .OUT(word_detection_2_out));
  word_detection word_detection_3 (
    .RESET(RESET), .CLOCK(CLOCK), .CHAR(KB_IN), .WORD_CODE(28'h778baf3), .OUT(word_detection_3_out));
  word_detection word_detection_4 (
    .RESET(RESET), .CLOCK(CLOCK), .CHAR(KB_IN), .WORD_CODE(28'h77c36e3), .OUT(word_detection_4_out));
  word_detection word_detection_5 (
    .RESET(RESET), .CLOCK(CLOCK), .CHAR(KB_IN), .WORD_CODE(28'h77d37ee), .OUT(word_detection_5_out));
  word_detection word_detection_6 (
    .RESET(RESET), .CLOCK(CLOCK), .CHAR(KB_IN), .WORD_CODE(28'h7793761), .OUT(word_detection_6_out));
  word_detection word_detection_7 (
    .RESET(RESET), .CLOCK(CLOCK), .CHAR(KB_IN), .WORD_CODE(28'hef96f), .OUT(word_detection_7_out));
  word_detection word_detection_8 (
    .RESET(RESET), .CLOCK(CLOCK), .CHAR(KB_IN), .WORD_CODE(28'h77b3473), .OUT(word_detection_8_out));
  word_detection word_detection_9 (
    .RESET(RESET), .CLOCK(CLOCK), .CHAR(KB_IN), .WORD_CODE(28'h77cb0f3), .OUT(word_detection_9_out));
  word_detection word_detection_10 (
    .RESET(RESET), .CLOCK(CLOCK), .CHAR(KB_IN), .WORD_CODE(28'hef769), .OUT(word_detection_10_out));
  word_detection word_detection_11 (
    .RESET(RESET), .CLOCK(CLOCK), .CHAR(KB_IN), .WORD_CODE(28'h77d3aef), .OUT(word_detection_11_out));
  word_detection word_detection_12 (
    .RESET(RESET), .CLOCK(CLOCK), .CHAR(KB_IN), .WORD_CODE(28'h77c36ea), .OUT(word_detection_12_out));
  word_detection word_detection_13 (
    .RESET(RESET), .CLOCK(CLOCK), .CHAR(KB_IN), .WORD_CODE(28'h77eb76a), .OUT(word_detection_13_out));
  word_detection word_detection_14 (
    .RESET(RESET), .CLOCK(CLOCK), .CHAR(KB_IN), .WORD_CODE(28'hefd6a), .OUT(word_detection_14_out));
  word_detection word_detection_15 (
    .RESET(RESET), .CLOCK(CLOCK), .CHAR(KB_IN), .WORD_CODE(28'hef3ea), .OUT(word_detection_15_out));
  word_detection word_detection_16 (
    .RESET(RESET), .CLOCK(CLOCK), .CHAR(KB_IN), .WORD_CODE(28'h77973ea), .OUT(word_detection_16_out));
  word_detection word_detection_17 (
    .RESET(RESET), .CLOCK(CLOCK), .CHAR(KB_IN), .WORD_CODE(28'hef66a), .OUT(word_detection_17_out));
  word_detection word_detection_18 (
    .RESET(RESET), .CLOCK(CLOCK), .CHAR(KB_IN), .WORD_CODE(28'h779766a), .OUT(word_detection_18_out));
  word_detection word_detection_19 (
    .RESET(RESET), .CLOCK(CLOCK), .CHAR(KB_IN), .WORD_CODE(28'hc3d30e4), .OUT(word_detection_19_out));
  or or_1 (or_1_out[0], word_detection_1_out, word_detection_3_out, word_detection_5_out, word_detection_7_out, word_detection_9_out, word_detection_11_out, word_detection_13_out, word_detection_15_out, word_detection_17_out, word_detection_19_out);
  or or_2 (or_1_out[1], word_detection_2_out, word_detection_3_out, word_detection_6_out, word_detection_7_out, word_detection_10_out, word_detection_11_out, word_detection_14_out, word_detection_15_out, word_detection_18_out, word_detection_19_out);
  or or_3 (or_1_out[2], word_detection_4_out, word_detection_5_out, word_detection_6_out, word_detection_7_out, word_detection_12_out, word_detection_13_out, word_detection_14_out, word_detection_15_out);
  or or_4 (or_1_out[3], word_detection_8_out, word_detection_9_out, word_detection_10_out, word_detection_11_out, word_detection_12_out, word_detection_13_out, word_detection_14_out, word_detection_15_out);
  or or_5 (or_1_out[4], word_detection_16_out, word_detection_17_out, word_detection_18_out, word_detection_19_out, 1'b0);
  // Probe on OP_OUT
  ROM #(.addrWidth(5)) rom_1 (.addr(or_1_out), .data(OP_OUT));  // open: sel

  // Notes on the sheet:
  //   01
  //   mov
  //   02
  //   add
  //   03
  //   sub
  //   04
  //   cmp
  //   05
  //   not
  //   06
  //   and
  //   or
  //   07
  //   shl
  //   08
  //   sar
  //   09
  //   0a
  //   in
  //   out
  //   0b
  //   jmp
  //   0c
  //   jnz
  //   0d
  //   jz
  //   0e
  //   jg
  //   0f
  //   jge
  //   10
  //   jl
  //   11
  //   jle
  //   12
  //   data
  //   13
  //   f
  //   e
  //   10
  //   11
  //   12
  //   13
  //   c
  //   a
  //   6
  //   b
  //   9
  //   d
  //   8
  //   7
  //   3
  //   1
  //   2
  //   5
  //   4
  //   contents of rom_1 (hex, n*v repeats v):
  //   0 1 2 3 4 5 6 7 8 9 a b c d e f 10 11 12 13
endmodule

module kb_num_decoder (
  input  [6:0] IN,
  output [3:0] OUT
);

  wire and_1_out, and_2_out, and_3_out, and_4_out, and_5_out, and_6_out, not_1_out, not_2_out, not_3_out,
       not_4_out, not_5_out, not_6_out, not_7_out;

  not not_1 (not_1_out, IN[4]);
  not not_2 (not_2_out, IN[4]);
  not not_3 (not_3_out, IN[1]);
  not not_4 (not_4_out, IN[6]);
  not not_5 (not_5_out, IN[0]);
  not not_6 (not_6_out, IN[6]);
  not not_7 (not_7_out, IN[0]);
  or or_1 (OUT[3], IN[3], IN[6]);
  and and_1 (and_1_out, not_1_out, IN[1], IN[0]);
  and and_2 (and_2_out, not_2_out, not_3_out, IN[0]);
  and and_3 (and_3_out, not_4_out, IN[1]);
  and and_4 (and_4_out, IN[1], not_5_out);
  and and_5 (and_5_out, not_6_out, IN[0]);
  and and_6 (and_6_out, IN[6], not_7_out);
  or or_2 (OUT[2], and_1_out, IN[2]);
  or or_3 (OUT[1], and_2_out, and_3_out, and_4_out);
  or or_4 (OUT[0], and_5_out, and_6_out);
endmodule

module ASSEMBLER (
  input  CLOCK,
  input  RESET,
  input  RESET_RAM
);

  wire and_1_out, and_2_out, and_3_out, and_4_out, and_5_out, comparator_1_eq, comparator_2_eq,
       comparator_4_gt, comparator_4_lt, not_1_out, or_1_out, or_3_out, or_4_out, or_5_out, or_6_out,
       s_r_ff_1_q, SP, WRITE;
  wire [1:0] counter_1_q;
  wire [3:0] kb_num_decoder_1_out, multiplexer_1_out, multiplexer_2_out, register_1_q, register_2_q,
       register_3_q, register_4_q;
  wire [6:0] demultiplexer_1_out0, demultiplexer_1_out1, keyboard_1_data;
  wire [7:0] op_keyboard_1_op_out;
  wire [15:0] counter_2_q;

  Keyboard #(.trigger("falling")) keyboard_1 (.clk(CLOCK), .clr(RESET), .data(keyboard_1_data));  // open: re, avail
  and and_1 (and_1_out, ~SP, CLOCK);  // AND_Gate
  // Probe on keyboard_1_data
  Comparator #(.width(7)) comparator_1 (.a(keyboard_1_data), .b(7'b0101111), .eq(comparator_1_eq));  // open: gt, lt
  Comparator #(.width(7)) comparator_2 (.a(keyboard_1_data), .b(7'b0100000), .eq(comparator_2_eq));  // open: gt, lt
  Comparator #(.width(7)) comparator_3 (.a(keyboard_1_data), .b(7'b0001010), .eq(WRITE));  // open: gt, lt
  or or_1 (or_1_out, RESET, WRITE);
  or or_2 (SP, comparator_2_eq, WRITE, comparator_1_eq);
  S_R_Flip_Flop #(.trigger("low")) s_r_ff_1 (
    .S(comparator_1_eq), .clk(1'b0), .R(comparator_2_eq), .Q(s_r_ff_1_q));  // open: Qn, preset, reset, en
  Demultiplexer #(.width(7), .enable("false")) demultiplexer_1 (
    .out0(demultiplexer_1_out0), .out1(demultiplexer_1_out1), .in(keyboard_1_data), .sel(s_r_ff_1_q));
  not not_1 (not_1_out, or_4_out);
  or or_3 (or_3_out, or_4_out, and_1_out);
  kb_num_decoder kb_num_decoder_1 (.IN(demultiplexer_1_out0), .OUT(kb_num_decoder_1_out));
  OP_KEYBOARD op_keyboard_1 (
    .KB_IN(demultiplexer_1_out1), .CLOCK(and_1_out), .RESET(or_1_out), .OP_OUT(op_keyboard_1_op_out));
  Comparator comparator_4 (
    .a(op_keyboard_1_op_out), .b({8{1'b0}}), .gt(comparator_4_gt), .lt(comparator_4_lt));  // open: eq
  Counter #(.width(2), .max('h3), .trigger("falling")) counter_1 (
    .load(or_4_out), .D(2'b10), .count(not_1_out), .Q(counter_1_q), .clk(or_3_out), .clr(or_1_out));  // open: carry
  or or_4 (or_4_out, comparator_4_gt, comparator_4_lt);
  and and_2 (and_2_out, ~counter_1_q[0], ~counter_1_q[1], and_1_out);  // AND_Gate
  and and_3 (and_3_out, counter_1_q[0], ~counter_1_q[1], and_1_out);  // AND_Gate
  and and_4 (and_4_out, ~counter_1_q[0], counter_1_q[1], and_1_out);  // AND_Gate
  and and_5 (and_5_out, counter_1_q[0], counter_1_q[1], and_1_out);
  Register #(.width(4)) register_1 (
    .D(multiplexer_1_out), .Q(register_1_q), .clk(or_5_out), .clr(or_1_out));  // open: en
  Multiplexer #(.width(4), .enable("false")) multiplexer_1 (
    .in0(kb_num_decoder_1_out), .in1(op_keyboard_1_op_out[7:4]), .out(multiplexer_1_out), .sel(s_r_ff_1_q));
  or or_5 (or_5_out, and_2_out, or_4_out);
  Register #(.width(4)) register_2 (
    .D(multiplexer_2_out), .Q(register_2_q), .clk(or_6_out), .clr(or_1_out));  // open: en
  Multiplexer #(.width(4), .enable("false")) multiplexer_2 (
    .in0(kb_num_decoder_1_out), .in1(op_keyboard_1_op_out[3:0]), .out(multiplexer_2_out), .sel(s_r_ff_1_q));
  or or_6 (or_6_out, and_3_out, or_4_out);
  Register #(.width(4)) register_3 (
    .D(kb_num_decoder_1_out), .Q(register_3_q), .clk(and_4_out), .clr(or_1_out));  // open: en
  Register #(.width(4)) register_4 (
    .D(kb_num_decoder_1_out), .Q(register_4_q), .clk(and_5_out), .clr(or_1_out));  // open: en
  Counter #(.width(16), .max('hffff), .trigger("falling")) counter_2 (
    .Q(counter_2_q), .clk(WRITE), .clr(RESET_RAM));  // open: load, D, count, carry
  RAM #(.addrWidth(16), .dataWidth(16), .bus("separate")) ram_1 (
    .addr(counter_2_q), .din({register_1_q, register_2_q, register_3_q, register_4_q}), .clk(WRITE),
    .clr(RESET_RAM));  // open: data, str, sel, ld
endmodule
